// Logisim project TCD_EDv1_6.circ as structural Verilog
module Matriz_de_led_Rol (
  input  MOSTRAR_MENSAGEM
);

  wire and_1_out, and_2_out, and_3_out, and_4_out, CLEAR_GERAL_out, CLK_out, contador_aux_1_check,
       contador_aux_1_lsb, contador_aux_1_middle, contador_aux_1_msb, keyboard_1_avail, not_1_out, not_2_out,
       or_1_out, or_2_out, PAUSE_out, velswitcher_2_ck_vel, VelSwitcher_out;
  wire [4:0] decod_ascii7bits_2_5x5matrixletter_1_col1, decod_ascii7bits_2_5x5matrixletter_1_col2,
       decod_ascii7bits_2_5x5matrixletter_1_col3, decod_ascii7bits_2_5x5matrixletter_1_col4,
       decod_ascii7bits_2_5x5matrixletter_1_col5, lol_1__1, lol_1__2, lol_1__3, lol_1__4, lol_1__5, lol_1__6,
       lol_1__7, lol_1__8, lol_1__9, lol_1__10, lol_1__11, lol_1__12, lol_1__13, lol_1__14, lol_1__15,
       lol_1__16, lol_1__17, lol_1__18, lol_1__19, lol_1__20, lol_1__21, lol_1__22, lol_1__23, lol_1__24,
       lol_1__25, lol_1__26, lol_1__27, lol_1__28, lol_1__29, lol_1__30, lol_1__31, lol_1__32, lol_1__33,
       lol_1__34, lol_1__35, lol_1__36, lol_1__37, lol_1__38, lol_1__39, lol_1__40, lol_1__41, lol_1__42,
       lol_1__43, lol_1__44, lol_1__45, lol_1__46, lol_1__47, lol_1__48, lol_1__49, lol_1__50, lol_1__51,
       lol_1__52, lol_1__53, lol_1__54, lol_1__55, lol_1__56, lol_1__57, lol_1__58, lol_1__59, lol_1__60,
       memoria_1_s, multiplex_ent_mem_1_s;
  wire [6:0] keyboard_1_data;

  Button VelSwitcher (.out(VelSwitcher_out));
  Button PAUSE (.out(PAUSE_out));
  and and_1 (and_1_out, MOSTRAR_MENSAGEM, ~keyboard_1_avail);  // AND_Gate
  Clock CLK (.out(CLK_out));
  and and_2 (and_2_out, ~and_1_out, keyboard_1_avail);  // AND_Gate
  and and_3 (and_3_out, ~and_1_out, ~keyboard_1_avail);  // AND_Gate
  Button CLEAR_GERAL (.out(CLEAR_GERAL_out));
  and and_4 (and_4_out, CLK_out, contador_aux_1_check);
  Keyboard keyboard_1 (
    .clk(and_4_out), .clr(CLEAR_GERAL_out), .avail(keyboard_1_avail), .data(keyboard_1_data));  // open: re
  Contador_AUX contador_aux_1 (
    .CLK(CLK_out), .CLEAR(CLEAR_GERAL_out), .ENABLE(and_2_out), .CHECK(contador_aux_1_check),
    .LSB(contador_aux_1_lsb), .MIDDLE(contador_aux_1_middle), .MSB(contador_aux_1_msb));
  not not_1 (not_1_out, keyboard_1_avail);
  or or_1 (or_1_out, CLEAR_GERAL_out, and_3_out);
  decod_ASCII7bits_2_5x5MatrixLetter decod_ascii7bits_2_5x5matrixletter_1 (
    ._7bits(keyboard_1_data), .COL1(decod_ascii7bits_2_5x5matrixletter_1_col1),
    .COL2(decod_ascii7bits_2_5x5matrixletter_1_col2), .COL3(decod_ascii7bits_2_5x5matrixletter_1_col3),
    .COL4(decod_ascii7bits_2_5x5matrixletter_1_col4), .COL5(decod_ascii7bits_2_5x5matrixletter_1_col5));
  Multiplex_Ent_Mem multiplex_ent_mem_1 (
    ._0(decod_ascii7bits_2_5x5matrixletter_1_col1), ._1(decod_ascii7bits_2_5x5matrixletter_1_col2),
    ._2(decod_ascii7bits_2_5x5matrixletter_1_col3), ._3(decod_ascii7bits_2_5x5matrixletter_1_col4),
    ._4(decod_ascii7bits_2_5x5matrixletter_1_col5), .A(contador_aux_1_msb), .B(contador_aux_1_middle),
    .C(contador_aux_1_lsb), .S(multiplex_ent_mem_1_s));
  memoria memoria_1 (
    .ENTRADA(multiplex_ent_mem_1_s), .CLEAR_CONT(or_1_out), .CLK(velswitcher_2_ck_vel), ._1R_0W(not_1_out),
    .CLEAR(CLEAR_GERAL_out), .S(memoria_1_s));
  VelSwitcher velswitcher_2 (
    .Vel_Switcher(VelSwitcher_out), .CK(CLK_out), .Pause(PAUSE_out), .CK_Vel(velswitcher_2_ck_vel));
  not not_2 (not_2_out, and_1_out);
  lol lol_1 (
    .CLK(velswitcher_2_ck_vel), .CLEAR(or_2_out), .ENTRADA(memoria_1_s), ._11(lol_1__11), ._21(lol_1__21),
    ._1(lol_1__1), ._12(lol_1__12), ._22(lol_1__22), ._2(lol_1__2), ._13(lol_1__13), ._23(lol_1__23),
    ._3(lol_1__3), ._14(lol_1__14), ._24(lol_1__24), ._4(lol_1__4), ._15(lol_1__15), ._25(lol_1__25),
    ._5(lol_1__5), ._6(lol_1__6), ._16(lol_1__16), ._26(lol_1__26), ._7(lol_1__7), ._17(lol_1__17),
    ._27(lol_1__27), ._8(lol_1__8), ._18(lol_1__18), ._28(lol_1__28), ._9(lol_1__9), ._19(lol_1__19),
    ._29(lol_1__29), ._10(lol_1__10), ._20(lol_1__20), ._30(lol_1__30), ._41(lol_1__41), ._51(lol_1__51),
    ._31(lol_1__31), ._42(lol_1__42), ._52(lol_1__52), ._32(lol_1__32), ._43(lol_1__43), ._53(lol_1__53),
    ._33(lol_1__33), ._44(lol_1__44), ._54(lol_1__54), ._34(lol_1__34), ._45(lol_1__45), ._55(lol_1__55),
    ._35(lol_1__35), ._36(lol_1__36), ._46(lol_1__46), ._56(lol_1__56), ._37(lol_1__37), ._47(lol_1__47),
    ._57(lol_1__57), ._38(lol_1__38), ._48(lol_1__48), ._58(lol_1__58), ._39(lol_1__39), ._49(lol_1__49),
    ._59(lol_1__59), ._40(lol_1__40), ._50(lol_1__50), ._60(lol_1__60));
  or or_2 (or_2_out, CLEAR_GERAL_out, not_2_out);
  DotMatrix #(.matrixcols(30), .matrixrows(5)) dotmatrix_1 (
    .col0(lol_1__60), .col1(lol_1__59), .col2(lol_1__58), .col3(lol_1__57), .col4(lol_1__56),
    .col5(lol_1__55), .col6(lol_1__54), .col7(lol_1__53), .col8(lol_1__52), .col9(lol_1__51),
    .col10(lol_1__50), .col11(lol_1__49), .col12(lol_1__48), .col13(lol_1__47), .col14(lol_1__46),
    .col15(lol_1__45), .col16(lol_1__44), .col17(lol_1__43), .col18(lol_1__42), .col19(lol_1__41),
    .col20(lol_1__40), .col21(lol_1__39), .col22(lol_1__38), .col23(lol_1__37), .col24(lol_1__36),
    .col25(lol_1__35), .col26(lol_1__34), .col27(lol_1__33), .col28(lol_1__32), .col29(lol_1__31));
  DotMatrix #(.matrixcols(30), .matrixrows(5)) dotmatrix_2 (
    .col0(lol_1__30), .col1(lol_1__29), .col2(lol_1__28), .col3(lol_1__27), .col4(lol_1__26),
    .col5(lol_1__25), .col6(lol_1__24), .col7(lol_1__23), .col8(lol_1__22), .col9(lol_1__21),
    .col10(lol_1__20), .col11(lol_1__19), .col12(lol_1__18), .col13(lol_1__17), .col14(lol_1__16),
    .col15(lol_1__15), .col16(lol_1__14), .col17(lol_1__13), .col18(lol_1__12), .col19(lol_1__11),
    .col20(lol_1__10), .col21(lol_1__9), .col22(lol_1__8), .col23(lol_1__7), .col24(lol_1__6),
    .col25(lol_1__5), .col26(lol_1__4), .col27(lol_1__3), .col28(lol_1__2), .col29(lol_1__1));

  // Notes on the sheet:
  //   TECLADO
endmodule

// REGIS
module lol (
  input  [4:0] ENTRADA,
  input  CLK,
  input  CLEAR,
  output [4:0] _1,
  output [4:0] _2,
  output [4:0] _3,
  output [4:0] _4,
  output [4:0] _5,
  output [4:0] _6,
  output [4:0] _7,
  output [4:0] _8,
  output [4:0] _9,
  output [4:0] _10,
  output [4:0] _31,
  output [4:0] _32,
  output [4:0] _33,
  output [4:0] _34,
  output [4:0] _35,
  output [4:0] _36,
  output [4:0] _37,
  output [4:0] _38,
  output [4:0] _39,
  output [4:0] _40,
  output [4:0] _11,
  output [4:0] _12,
  output [4:0] _13,
  output [4:0] _14,
  output [4:0] _15,
  output [4:0] _16,
  output [4:0] _17,
  output [4:0] _18,
  output [4:0] _19,
  output [4:0] _20,
  output [4:0] _41,
  output [4:0] _42,
  output [4:0] _43,
  output [4:0] _44,
  output [4:0] _45,
  output [4:0] _46,
  output [4:0] _47,
  output [4:0] _48,
  output [4:0] _49,
  output [4:0] _50,
  output [4:0] _21,
  output [4:0] _22,
  output [4:0] _23,
  output [4:0] _24,
  output [4:0] _25,
  output [4:0] _26,
  output [4:0] _27,
  output [4:0] _28,
  output [4:0] _29,
  output [4:0] _30,
  output [4:0] _51,
  output [4:0] _52,
  output [4:0] _53,
  output [4:0] _54,
  output [4:0] _55,
  output [4:0] _56,
  output [4:0] _57,
  output [4:0] _58,
  output [4:0] _59,
  output [4:0] _60
);

  wire [4:0] shift_register_1_out;

  Shift_Register #(.width(5), .length(30)) shift_register_1 (
    .in(ENTRADA), .clk(CLK), .out(shift_register_1_out), .clr(CLEAR), .q0(_1), .q1(_2), .q2(_3), .q3(_4),
    .q4(_5), .q5(_6), .q6(_7), .q7(_8), .q8(_9), .q9(_10), .q10(_11), .q11(_12), .q12(_13), .q13(_14),
    .q14(_15), .q15(_16), .q16(_17), .q17(_18), .q18(_19), .q19(_20), .q20(_21), .q21(_22), .q22(_23),
    .q23(_24), .q24(_25), .q25(_26), .q26(_27), .q27(_28), .q28(_29), .q29(_30));  // open: shift, load, d0, d1, d2, d3, d4, d5, d6, d7, d8, d9, d10, d11, d12, d13, d14, d15, d16, d17, d18, d19, d20, d21, d22, d23, d24, d25, d26, d27, d28, d29
  Shift_Register #(.width(5), .length(30)) shift_register_2 (
    .in(shift_register_1_out), .clk(CLK), .clr(CLEAR), .q0(_31), .q1(_32), .q2(_33), .q3(_34), .q4(_35),
    .q5(_36), .q6(_37), .q7(_38), .q8(_39), .q9(_40), .q10(_41), .q11(_42), .q12(_43), .q13(_44), .q14(_45),
    .q15(_46), .q16(_47), .q17(_48), .q18(_49), .q19(_50), .q20(_51), .q21(_52), .q22(_53), .q23(_54),
    .q24(_55), .q25(_56), .q26(_57), .q27(_58), .q28(_59), .q29(_60));  // open: shift, out, load, d0, d1, d2, d3, d4, d5, d6, d7, d8, d9, d10, d11, d12, d13, d14, d15, d16, d17, d18, d19, d20, d21, d22, d23, d24, d25, d26, d27, d28, d29
endmodule

module Multi (
  input  [4:0] E0,
  input  [4:0] E1,
  input  A,
  output [4:0] S
);

  wire [4:0] and_1_out, and_2_out;

  assign and_1_out = E0 & ~{5{A}};  // AND_Gate and_1, 5 bits wide
  assign and_2_out = E1 & {5{A}};  // AND_Gate and_2, 5 bits wide
  assign S = and_1_out | and_2_out;  // OR_Gate or_1, 5 bits wide
endmodule

module GPC (
  input  [4:0] E0,
  input  [4:0] E1,
  input  [4:0] E2,
  output [4:0] S0,
  output [4:0] S1,
  output [4:0] S2,
  output [4:0] S3,
  output [4:0] S4
);

  wire [4:0] and_1_out, and_2_out, and_3_out, and_4_out, and_5_out, and_6_out, not_1_out, not_2_out,
       not_3_out, not_4_out, not_5_out;

  assign not_1_out = ~E0;  // NOT_Gate not_1, 5 bits wide
  assign not_2_out = ~E1;  // NOT_Gate not_2, 5 bits wide
  assign not_3_out = ~E2;  // NOT_Gate not_3, 5 bits wide
  assign not_4_out = ~E1;  // NOT_Gate not_4, 5 bits wide
  assign not_5_out = ~E2;  // NOT_Gate not_5, 5 bits wide
  assign and_1_out = not_1_out & not_2_out & not_3_out;  // AND_Gate and_1, 5 bits wide
  assign and_2_out = E0 & E1;  // AND_Gate and_2, 5 bits wide
  assign and_3_out = not_4_out & E2;  // AND_Gate and_3, 5 bits wide
  assign and_4_out = E0 & E1;  // AND_Gate and_4, 5 bits wide
  assign and_5_out = E1 & not_5_out;  // AND_Gate and_5, 5 bits wide
  assign and_6_out = E0 & E1;  // AND_Gate and_6, 5 bits wide
  assign S3 = E1 & E2;  // AND_Gate and_7, 5 bits wide
  assign S0 = and_1_out | and_2_out;  // OR_Gate or_1, 5 bits wide
  assign S1 = and_3_out | and_4_out;  // OR_Gate or_2, 5 bits wide
  assign S2 = and_5_out | and_6_out;  // OR_Gate or_3, 5 bits wide

  assign S4 = E0;
endmodule

// MEM
module memoria (
  input  [4:0] ENTRADA,
  input  CLEAR_CONT,
  input  CLK,
  input  _1R_0W,
  input  CLEAR,
  output [4:0] S
);

  wire not_1_out;
  wire [7:0] counter_1_q;

  assign S = not_1_out ? ENTRADA : 5'bz;  // Controlled_Buffer controlled_buffer_1
  not not_1 (not_1_out, _1R_0W);
  Counter #(.max('ha0), .trigger("falling")) counter_1 (
    .Q(counter_1_q), .clk(CLK), .clr(CLEAR_CONT));  // open: load, D, count, carry
  RAM #(.dataWidth(5)) ram_1 (.addr(counter_1_q), .data(S), .sel(1'b1), .clk(CLK), .ld(_1R_0W), .clr(CLEAR));
endmodule

// Mux_EM
module Multiplex_Ent_Mem (
  input  [4:0] _0,
  input  [4:0] _1,
  input  [4:0] _2,
  input  [4:0] _3,
  input  [4:0] _4,
  input  A,
  input  B,
  input  C,
  output [4:0] S
);

  wire [4:0] and_1_out, and_2_out, and_3_out, and_4_out, and_5_out, gpc_1_s0, gpc_1_s1, gpc_1_s2, gpc_1_s3,
       gpc_1_s4;

  GPC gpc_1 (
    .E0({5{A}}), .E1({5{B}}), .E2({5{C}}), .S0(gpc_1_s0), .S1(gpc_1_s1), .S2(gpc_1_s2), .S3(gpc_1_s3),
    .S4(gpc_1_s4));
  assign and_1_out = _0 & gpc_1_s0;  // AND_Gate and_1, 5 bits wide
  assign and_2_out = _1 & gpc_1_s1;  // AND_Gate and_2, 5 bits wide
  assign and_3_out = _2 & gpc_1_s2;  // AND_Gate and_3, 5 bits wide
  assign and_4_out = _3 & gpc_1_s3;  // AND_Gate and_4, 5 bits wide
  assign and_5_out = _4 & gpc_1_s4;  // AND_Gate and_5, 5 bits wide
  assign S = and_1_out | and_2_out | and_3_out | and_4_out | and_5_out;  // OR_Gate or_1, 5 bits wide
endmodule

// CNT
module Contador_AUX (
  input  CLK,
  input  CLEAR,
  input  ENABLE,
  output CHECK,
  output LSB,
  output MSB,
  output MIDDLE
);

  wire and_2_out, or_1_out;

  and and_1 (CHECK, ~LSB, ~MIDDLE, MSB);  // AND_Gate
  T_Flip_Flop #(.trigger("falling")) t_ff_1 (
    .clk(CLK), .T(1'b1), .Q(LSB), .reset(or_1_out), .en(ENABLE));  // open: Qn, preset
  or or_1 (or_1_out, CLEAR, and_2_out);
  T_Flip_Flop #(.trigger("falling")) t_ff_2 (
    .clk(LSB), .T(1'b1), .Q(MIDDLE), .reset(or_1_out), .en(ENABLE));  // open: Qn, preset
  and and_2 (and_2_out, LSB, ~MIDDLE, MSB);  // AND_Gate
  T_Flip_Flop #(.trigger("falling")) t_ff_3 (
    .clk(MIDDLE), .T(1'b1), .Q(MSB), .reset(or_1_out), .en(ENABLE));  // open: Qn, preset
endmodule

// ML1
module ASCII_7bits_2_5x5_Letter (
  input  B6,
  input  B5,
  input  B4,
  input  B3,
  input  B2,
  input  B1,
  input  B0,
  output C_11,
  output C_12,
  output C_13,
  output C_14,
  output C_15,
  output C_21,
  output C_22,
  output C_23,
  output C_24,
  output C_25
);

  wire and_1_out, and_2_out, and_3_out, and_4_out, and_5_out, and_6_out, and_7_out, and_8_out, and_9_out,
       and_10_out, and_11_out, and_12_out, and_13_out, and_14_out, and_15_out, and_16_out, and_17_out,
       and_18_out, and_19_out, and_20_out, and_21_out, and_22_out, and_23_out, and_24_out, and_25_out,
       and_26_out, and_27_out, and_28_out, and_29_out, and_30_out, and_31_out, and_32_out, and_33_out,
       and_34_out, and_35_out, and_36_out, and_37_out, and_38_out, and_39_out, and_40_out, and_41_out,
       and_42_out, and_43_out, and_44_out, and_45_out, and_46_out, and_47_out, and_48_out, and_49_out,
       and_50_out, and_51_out, and_52_out, and_53_out, and_54_out, and_55_out, and_56_out, and_57_out,
       and_58_out, and_59_out, and_60_out, and_61_out, and_62_out, and_63_out, and_64_out, and_65_out,
       and_66_out, and_67_out, and_68_out, and_69_out, and_70_out, and_71_out, and_72_out, and_73_out,
       and_74_out, and_75_out, and_76_out, and_77_out, and_78_out, and_79_out, and_80_out, and_81_out,
       and_82_out, and_83_out, and_84_out, and_85_out, and_86_out, and_87_out, and_88_out, and_89_out,
       and_90_out, and_91_out, and_92_out, and_93_out, and_94_out, and_95_out, and_96_out, and_97_out,
       and_98_out, and_99_out, and_100_out, and_101_out, and_102_out, and_103_out, and_104_out, and_105_out,
       and_106_out, and_107_out, and_108_out, and_109_out, and_110_out, and_111_out, and_112_out,
       and_113_out, and_114_out, and_115_out, and_116_out, and_117_out, and_118_out, and_119_out,
       and_120_out, not_1_out, not_2_out, not_3_out, not_4_out, not_5_out, not_6_out, not_7_out, not_8_out,
       not_9_out, not_10_out, not_11_out, not_12_out, not_13_out, not_14_out, not_15_out, not_16_out,
       not_17_out, not_18_out, not_19_out, not_20_out, not_21_out, not_22_out, not_23_out, not_24_out,
       not_25_out, not_26_out, not_27_out, not_28_out, not_29_out, not_30_out, not_31_out, not_32_out,
       not_33_out, not_34_out, not_35_out, not_36_out, not_37_out, not_38_out, not_39_out, not_40_out,
       not_41_out, not_42_out, not_43_out, not_44_out, not_45_out, not_46_out, not_47_out, not_48_out,
       not_49_out, not_50_out, not_51_out, not_52_out, not_53_out, not_54_out, not_55_out, not_56_out,
       not_57_out, not_58_out, not_59_out, not_60_out, not_61_out, not_62_out, not_63_out, not_64_out,
       not_65_out, not_66_out, not_67_out, not_68_out, not_69_out, not_70_out, not_71_out, not_72_out,
       not_73_out, not_74_out, not_75_out, not_76_out, not_77_out, not_78_out, not_79_out, not_80_out,
       not_81_out, not_82_out, not_83_out, not_84_out, not_85_out, not_86_out, not_87_out, not_88_out,
       not_89_out, not_90_out, not_91_out, not_92_out, not_93_out, not_94_out, not_95_out, not_96_out,
       not_97_out, not_98_out, not_99_out, not_100_out, not_101_out, not_102_out, not_103_out, not_104_out,
       not_105_out, not_106_out, not_107_out, not_108_out, not_109_out, not_110_out, not_111_out,
       not_112_out, not_113_out, not_114_out, not_115_out, not_116_out, not_117_out, not_118_out,
       not_119_out, not_120_out, not_121_out, not_122_out, not_123_out, not_124_out, not_125_out,
       not_126_out, not_127_out, not_128_out, not_129_out, not_130_out, not_131_out, not_132_out,
       not_133_out, not_134_out, not_135_out, not_136_out, not_137_out, not_138_out, not_139_out,
       not_140_out, not_141_out, not_142_out, not_143_out, not_144_out, not_145_out, not_146_out,
       not_147_out, not_148_out, not_149_out, not_150_out, not_151_out, not_152_out, not_153_out,
       not_154_out, not_155_out, not_156_out, not_157_out, not_158_out, not_159_out, not_160_out,
       not_161_out, not_162_out, not_163_out, not_164_out, not_165_out, not_166_out, not_167_out,
       not_168_out, not_169_out, not_170_out, not_171_out, not_172_out, not_173_out, not_174_out,
       not_175_out, not_176_out, not_177_out, not_178_out, not_179_out, not_180_out, not_181_out,
       not_182_out, not_183_out, not_184_out, not_185_out, not_186_out, not_187_out, not_188_out,
       not_189_out, not_190_out, not_191_out, not_192_out, not_193_out, not_194_out, not_195_out,
       not_196_out, not_197_out, not_198_out, not_199_out, not_200_out, not_201_out, not_202_out,
       not_203_out, not_204_out, not_205_out, not_206_out, not_207_out, not_208_out, not_209_out,
       not_210_out, not_211_out, not_212_out, not_213_out, not_214_out, not_215_out, not_216_out,
       not_217_out, not_218_out, not_219_out, not_220_out, not_221_out, not_222_out, not_223_out,
       not_224_out, not_225_out, not_226_out, not_227_out, not_228_out, not_229_out, not_230_out,
       not_231_out, not_232_out, not_233_out, not_234_out, not_235_out, not_236_out, not_237_out,
       not_238_out, not_239_out, not_240_out, not_241_out, not_242_out, not_243_out, not_244_out,
       not_245_out, not_246_out, not_247_out, not_248_out, not_249_out, not_250_out, not_251_out,
       not_252_out, not_253_out, not_254_out, not_255_out, not_256_out, not_257_out, not_258_out,
       not_259_out, not_260_out, not_261_out, not_262_out, not_263_out;

  not not_1 (not_1_out, B5);
  not not_2 (not_2_out, B3);
  not not_3 (not_3_out, B2);
  not not_4 (not_4_out, B1);
  not not_5 (not_5_out, B4);
  not not_6 (not_6_out, B1);
  not not_7 (not_7_out, B0);
  not not_8 (not_8_out, B6);
  not not_9 (not_9_out, B3);
  not not_10 (not_10_out, B0);
  not not_11 (not_11_out, B6);
  not not_12 (not_12_out, B3);
  not not_13 (not_13_out, B1);
  not not_14 (not_14_out, B6);
  not not_15 (not_15_out, B3);
  not not_16 (not_16_out, B2);
  not not_17 (not_17_out, B6);
  not not_18 (not_18_out, B2);
  not not_19 (not_19_out, B1);
  not not_20 (not_20_out, B3);
  not not_21 (not_21_out, B2);
  not not_22 (not_22_out, B1);
  not not_23 (not_23_out, B4);
  not not_24 (not_24_out, B2);
  not not_25 (not_25_out, B1);
  not not_26 (not_26_out, B0);
  not not_27 (not_27_out, B2);
  not not_28 (not_28_out, B1);
  not not_29 (not_29_out, B6);
  not not_30 (not_30_out, B3);
  not not_31 (not_31_out, B0);
  not not_32 (not_32_out, B6);
  not not_33 (not_33_out, B2);
  not not_34 (not_34_out, B1);
  not not_35 (not_35_out, B0);
  not not_36 (not_36_out, B5);
  not not_37 (not_37_out, B3);
  not not_38 (not_38_out, B2);
  not not_39 (not_39_out, B1);
  not not_40 (not_40_out, B3);
  not not_41 (not_41_out, B2);
  not not_42 (not_42_out, B0);
  not not_43 (not_43_out, B4);
  not not_44 (not_44_out, B5);
  not not_45 (not_45_out, B4);
  not not_46 (not_46_out, B5);
  not not_47 (not_47_out, B1);
  not not_48 (not_48_out, B4);
  not not_49 (not_49_out, B2);
  not not_50 (not_50_out, B1);
  not not_51 (not_51_out, B0);
  not not_52 (not_52_out, B6);
  not not_53 (not_53_out, B3);
  not not_54 (not_54_out, B0);
  not not_55 (not_55_out, B6);
  not not_56 (not_56_out, B3);
  not not_57 (not_57_out, B2);
  not not_58 (not_58_out, B6);
  not not_59 (not_59_out, B1);
  not not_60 (not_60_out, B3);
  not not_61 (not_61_out, B2);
  not not_62 (not_62_out, B1);
  not not_63 (not_63_out, B4);
  not not_64 (not_64_out, B3);
  not not_65 (not_65_out, B6);
  not not_66 (not_66_out, B5);
  not not_67 (not_67_out, B3);
  not not_68 (not_68_out, B2);
  not not_69 (not_69_out, B5);
  not not_70 (not_70_out, B3);
  not not_71 (not_71_out, B2);
  not not_72 (not_72_out, B1);
  not not_73 (not_73_out, B6);
  not not_74 (not_74_out, B5);
  not not_75 (not_75_out, B4);
  not not_76 (not_76_out, B2);
  not not_77 (not_77_out, B1);
  not not_78 (not_78_out, B0);
  not not_79 (not_79_out, B3);
  not not_80 (not_80_out, B2);
  not not_81 (not_81_out, B1);
  not not_82 (not_82_out, B0);
  not not_83 (not_83_out, B6);
  not not_84 (not_84_out, B3);
  not not_85 (not_85_out, B0);
  not not_86 (not_86_out, B6);
  not not_87 (not_87_out, B2);
  not not_88 (not_88_out, B1);
  not not_89 (not_89_out, B3);
  not not_90 (not_90_out, B2);
  not not_91 (not_91_out, B1);
  not not_92 (not_92_out, B3);
  not not_93 (not_93_out, B2);
  not not_94 (not_94_out, B0);
  not not_95 (not_95_out, B3);
  not not_96 (not_96_out, B5);
  not not_97 (not_97_out, B3);
  not not_98 (not_98_out, B1);
  not not_99 (not_99_out, B6);
  not not_100 (not_100_out, B3);
  not not_101 (not_101_out, B6);
  not not_102 (not_102_out, B6);
  not not_103 (not_103_out, B2);
  not not_104 (not_104_out, B1);
  not not_105 (not_105_out, B3);
  not not_106 (not_106_out, B1);
  not not_107 (not_107_out, B4);
  not not_108 (not_108_out, B3);
  not not_109 (not_109_out, B2);
  not not_110 (not_110_out, B4);
  not not_111 (not_111_out, B1);
  not not_112 (not_112_out, B0);
  not not_113 (not_113_out, B4);
  not not_114 (not_114_out, B3);
  not not_115 (not_115_out, B3);
  not not_116 (not_116_out, B1);
  not not_117 (not_117_out, B4);
  not not_118 (not_118_out, B4);
  not not_119 (not_119_out, B2);
  not not_120 (not_120_out, B1);
  not not_121 (not_121_out, B5);
  not not_122 (not_122_out, B3);
  not not_123 (not_123_out, B5);
  not not_124 (not_124_out, B6);
  not not_125 (not_125_out, B4);
  not not_126 (not_126_out, B0);
  not not_127 (not_127_out, B6);
  not not_128 (not_128_out, B2);
  not not_129 (not_129_out, B6);
  not not_130 (not_130_out, B0);
  not not_131 (not_131_out, B4);
  not not_132 (not_132_out, B2);
  not not_133 (not_133_out, B0);
  not not_134 (not_134_out, B3);
  not not_135 (not_135_out, B5);
  not not_136 (not_136_out, B0);
  not not_137 (not_137_out, B0);
  not not_138 (not_138_out, B6);
  not not_139 (not_139_out, B1);
  not not_140 (not_140_out, B0);
  not not_141 (not_141_out, B6);
  not not_142 (not_142_out, B3);
  not not_143 (not_143_out, B2);
  not not_144 (not_144_out, B1);
  not not_145 (not_145_out, B0);
  not not_146 (not_146_out, B0);
  not not_147 (not_147_out, B0);
  not not_148 (not_148_out, B5);
  not not_149 (not_149_out, B3);
  not not_150 (not_150_out, B2);
  not not_151 (not_151_out, B0);
  not not_152 (not_152_out, B5);
  not not_153 (not_153_out, B4);
  not not_154 (not_154_out, B3);
  not not_155 (not_155_out, B1);
  not not_156 (not_156_out, B6);
  not not_157 (not_157_out, B3);
  not not_158 (not_158_out, B0);
  not not_159 (not_159_out, B4);
  not not_160 (not_160_out, B3);
  not not_161 (not_161_out, B0);
  not not_162 (not_162_out, B4);
  not not_163 (not_163_out, B3);
  not not_164 (not_164_out, B1);
  not not_165 (not_165_out, B4);
  not not_166 (not_166_out, B2);
  not not_167 (not_167_out, B1);
  not not_168 (not_168_out, B0);
  not not_169 (not_169_out, B2);
  not not_170 (not_170_out, B6);
  not not_171 (not_171_out, B3);
  not not_172 (not_172_out, B2);
  not not_173 (not_173_out, B6);
  not not_174 (not_174_out, B1);
  not not_175 (not_175_out, B5);
  not not_176 (not_176_out, B6);
  not not_177 (not_177_out, B3);
  not not_178 (not_178_out, B1);
  not not_179 (not_179_out, B6);
  not not_180 (not_180_out, B2);
  not not_181 (not_181_out, B1);
  not not_182 (not_182_out, B3);
  not not_183 (not_183_out, B2);
  not not_184 (not_184_out, B0);
  not not_185 (not_185_out, B4);
  not not_186 (not_186_out, B3);
  not not_187 (not_187_out, B1);
  not not_188 (not_188_out, B5);
  not not_189 (not_189_out, B0);
  not not_190 (not_190_out, B5);
  not not_191 (not_191_out, B1);
  not not_192 (not_192_out, B1);
  not not_193 (not_193_out, B0);
  not not_194 (not_194_out, B6);
  not not_195 (not_195_out, B3);
  not not_196 (not_196_out, B2);
  not not_197 (not_197_out, B1);
  not not_198 (not_198_out, B0);
  not not_199 (not_199_out, B3);
  not not_200 (not_200_out, B2);
  not not_201 (not_201_out, B1);
  not not_202 (not_202_out, B5);
  not not_203 (not_203_out, B3);
  not not_204 (not_204_out, B2);
  not not_205 (not_205_out, B5);
  not not_206 (not_206_out, B3);
  not not_207 (not_207_out, B1);
  not not_208 (not_208_out, B0);
  not not_209 (not_209_out, B2);
  not not_210 (not_210_out, B0);
  not not_211 (not_211_out, B4);
  not not_212 (not_212_out, B3);
  not not_213 (not_213_out, B4);
  not not_214 (not_214_out, B1);
  not not_215 (not_215_out, B6);
  not not_216 (not_216_out, B3);
  not not_217 (not_217_out, B6);
  not not_218 (not_218_out, B6);
  not not_219 (not_219_out, B2);
  not not_220 (not_220_out, B0);
  not not_221 (not_221_out, B3);
  not not_222 (not_222_out, B2);
  not not_223 (not_223_out, B3);
  not not_224 (not_224_out, B1);
  not not_225 (not_225_out, B0);
  not not_226 (not_226_out, B5);
  not not_227 (not_227_out, B4);
  and and_1 (and_1_out, not_226_out, not_227_out, not_228_out);
  not not_228 (not_228_out, B3);
  and and_2 (and_2_out, not_1_out, not_2_out, not_3_out, not_4_out);
  not not_229 (not_229_out, B4);
  and and_3 (and_3_out, not_229_out, B1, B0);
  not not_230 (not_230_out, B5);
  not not_231 (not_231_out, B4);
  and and_4 (and_4_out, not_230_out, not_231_out, B2);
  not not_232 (not_232_out, B4);
  and and_5 (and_5_out, not_232_out, B2, not_233_out);
  not not_233 (not_233_out, B1);
  and and_6 (and_6_out, not_5_out, B3, not_6_out, not_7_out);
  and and_7 (and_7_out, B4, not_234_out, not_235_out);
  not not_234 (not_234_out, B2);
  not not_235 (not_235_out, B0);
  and and_8 (and_8_out, not_8_out, B5, not_9_out, B1, not_10_out);
  and and_9 (and_9_out, not_11_out, B5, not_12_out, B2, not_13_out, B0);
  and and_10 (and_10_out, not_14_out, B5, B4, not_15_out, not_16_out);
  and and_11 (and_11_out, not_17_out, B5, B4, not_18_out, not_19_out);
  not not_236 (not_236_out, B4);
  and and_12 (and_12_out, B6, not_236_out, not_237_out);
  not not_237 (not_237_out, B0);
  and and_13 (and_13_out, B6, not_20_out, not_21_out, not_22_out);
  not not_238 (not_238_out, B5);
  not not_239 (not_239_out, B3);
  and and_14 (and_14_out, not_238_out, not_239_out, not_240_out);
  not not_240 (not_240_out, B2);
  not not_241 (not_241_out, B4);
  and and_15 (and_15_out, not_241_out, B1, B0);
  not not_242 (not_242_out, B5);
  and and_16 (and_16_out, not_242_out, not_243_out, B2);
  not not_243 (not_243_out, B4);
  not not_244 (not_244_out, B4);
  and and_17 (and_17_out, not_244_out, not_245_out, B2);
  not not_245 (not_245_out, B3);
  not not_246 (not_246_out, B5);
  and and_18 (and_18_out, not_246_out, B2, B0);
  and and_19 (and_19_out, not_23_out, B3, not_24_out, not_25_out, not_26_out);
  and and_20 (and_20_out, B3, not_27_out, B1, B0);
  and and_21 (and_21_out, B3, B2, not_28_out, B0);
  and and_22 (and_22_out, not_29_out, B5, not_30_out, B1, not_31_out);
  and and_23 (and_23_out, not_32_out, B5, B4, not_33_out, not_34_out, not_35_out);
  and and_24 (and_24_out, B6, not_247_out, not_248_out);
  not not_247 (not_247_out, B3);
  not not_248 (not_248_out, B2);
  not not_249 (not_249_out, B4);
  and and_25 (and_25_out, B6, not_249_out, B2);
  and and_26 (and_26_out, B6, B2, B0);
  and and_27 (and_27_out, not_36_out, not_37_out, not_38_out, not_39_out);
  and and_28 (and_28_out, not_40_out, not_41_out, B1, not_42_out);
  and and_29 (and_29_out, not_43_out, B1, B0);
  and and_30 (and_30_out, not_44_out, not_45_out, B2);
  and and_31 (and_31_out, not_46_out, B2, B0);
  and and_32 (and_32_out, B2, not_47_out, B0);
  and and_33 (and_33_out, not_48_out, B3, not_49_out, not_50_out, not_51_out);
  and and_34 (and_34_out, B3, B2, B0);
  and and_35 (and_35_out, not_52_out, B5, not_53_out, B2, not_54_out);
  and and_36 (and_36_out, not_55_out, B5, B4, not_56_out, not_57_out);
  and and_37 (and_37_out, not_58_out, B5, B4, not_59_out, B0);
  and and_38 (and_38_out, B6, not_60_out, not_61_out, not_62_out);
  and and_39 (and_39_out, B6, not_63_out, B2);
  and and_40 (and_40_out, B6, not_64_out, B2, B1);
  and and_41 (and_41_out, not_65_out, not_66_out, not_67_out, not_68_out);
  and and_42 (and_42_out, not_69_out, not_70_out, not_71_out, not_72_out);
  not not_250 (not_250_out, B4);
  not not_251 (not_251_out, B3);
  and and_43 (and_43_out, not_250_out, not_251_out, B1);
  and and_44 (and_44_out, not_73_out, not_74_out, B1, B0);
  not not_252 (not_252_out, B5);
  not not_253 (not_253_out, B4);
  and and_45 (and_45_out, not_252_out, not_253_out, B2);
  not not_254 (not_254_out, B1);
  and and_46 (and_46_out, B2, not_254_out, B0);
  and and_47 (and_47_out, not_75_out, B3, not_76_out, not_77_out, not_78_out);
  and and_48 (and_48_out, B3, B1, B0);
  and and_49 (and_49_out, B4, not_79_out, not_80_out, not_81_out, not_82_out);
  and and_50 (and_50_out, not_83_out, B5, not_84_out, B2, not_85_out);
  and and_51 (and_51_out, not_86_out, B5, B4, B3, not_87_out, not_88_out);
  and and_52 (and_52_out, B6, not_89_out, not_90_out, not_91_out);
  and and_53 (and_53_out, B6, not_92_out, not_93_out, not_94_out);
  and and_54 (and_54_out, B6, not_255_out, B2);
  not not_255 (not_255_out, B4);
  and and_55 (and_55_out, B6, not_95_out, B2, B1);
  not not_256 (not_256_out, B5);
  and and_56 (and_56_out, not_256_out, not_257_out);
  not not_257 (not_257_out, B0);
  not not_258 (not_258_out, B4);
  and and_57 (and_57_out, not_258_out, B1, B0);
  not not_259 (not_259_out, B3);
  and and_58 (and_58_out, not_259_out, B2);
  not not_260 (not_260_out, B2);
  and and_59 (and_59_out, B3, not_260_out, not_261_out);
  not not_261 (not_261_out, B0);
  and and_60 (and_60_out, not_96_out, B4, not_97_out, not_98_out);
  and and_61 (and_61_out, B4, not_262_out);
  not not_262 (not_262_out, B0);
  and and_62 (and_62_out, not_99_out, B5, not_100_out, B1);
  and and_63 (and_63_out, not_101_out, B5, B4, B2, B1);
  and and_64 (and_64_out, not_102_out, B5, B4, B3, not_103_out, not_104_out);
  and and_65 (and_65_out, B6, not_263_out);
  not not_263 (not_263_out, B0);
  and and_66 (and_66_out, B6, B4, not_105_out, not_106_out);
  and and_67 (and_67_out, not_107_out, not_108_out, not_109_out, B1);
  and and_68 (and_68_out, not_110_out, B2, not_111_out, not_112_out);
  and and_69 (and_69_out, not_113_out, not_114_out, B2, B0);
  and and_70 (and_70_out, not_115_out, B2, not_116_out, B0);
  and and_71 (and_71_out, not_117_out, B2, B1, B0);
  and and_72 (and_72_out, not_118_out, B3, not_119_out, not_120_out, B0);
  and and_73 (and_73_out, not_121_out, B4, not_122_out, B0);
  and and_74 (and_74_out, not_123_out, B4, B3, B1);
  and and_75 (and_75_out, not_124_out, B5, not_125_out, B3, B2, not_126_out);
  and and_76 (and_76_out, not_127_out, B5, B4, not_128_out);
  and and_77 (and_77_out, not_129_out, B5, B4, B1, not_130_out);
  and and_78 (and_78_out, B6, not_131_out, not_132_out, B1, not_133_out);
  and and_79 (and_79_out, B6, B4, not_134_out, B0);
  and and_80 (and_80_out, B6, B4, B3, B1);
  and and_81 (and_81_out, not_135_out, B4, B3, not_136_out);
  and and_82 (and_82_out, B4, B3, B1, not_137_out);
  and and_83 (and_83_out, not_138_out, B5, B3, B2, not_139_out, not_140_out);
  and and_84 (and_84_out, not_141_out, B5, B4, not_142_out, not_143_out, not_144_out, not_145_out);
  and and_85 (and_85_out, B6, B4, B2, B1, not_146_out);
  and and_86 (and_86_out, B6, B4, B3, not_147_out);
  and and_87 (and_87_out, not_148_out, not_149_out, not_150_out, not_151_out);
  and and_88 (and_88_out, not_152_out, not_153_out, not_154_out, not_155_out, B0);
  and and_89 (and_89_out, not_156_out, not_157_out, B1, not_158_out);
  and and_90 (and_90_out, not_159_out, not_160_out, B1, not_161_out);
  and and_91 (and_91_out, not_162_out, not_163_out, B2, not_164_out, B0);
  and and_92 (and_92_out, not_165_out, B3, not_166_out, not_167_out, not_168_out);
  and and_93 (and_93_out, B3, not_169_out, B1, B0);
  and and_94 (and_94_out, not_170_out, B4, not_171_out, not_172_out, B1);
  and and_95 (and_95_out, not_173_out, B4, B3, not_174_out, B0);
  and and_96 (and_96_out, not_175_out, B4, B3, B1, B0);
  and and_97 (and_97_out, not_176_out, B5, B4, not_177_out, B2, not_178_out);
  and and_98 (and_98_out, not_179_out, B5, B4, B3, not_180_out, not_181_out);
  and and_99 (and_99_out, B6, not_182_out, not_183_out, not_184_out);
  and and_100 (and_100_out, B6, not_185_out, not_186_out, not_187_out, B0);
  and and_101 (and_101_out, B6, B4, B3, B2, B0);
  and and_102 (and_102_out, not_188_out, B3, B2, B1, not_189_out);
  and and_103 (and_103_out, not_190_out, B4, B3, not_191_out);
  and and_104 (and_104_out, B4, B3, B2, not_192_out);
  and and_105 (and_105_out, B4, B3, B2, not_193_out);
  and and_106 (and_106_out, not_194_out, B5, B4, not_195_out, not_196_out, not_197_out, B0);
  and and_107 (and_107_out, B6, B3, B2, B1, not_198_out);
  and and_108 (and_108_out, B6, B4, not_199_out, not_200_out, B1, B0);
  and and_109 (and_109_out, B6, B4, B3, not_201_out);
  and and_110 (and_110_out, not_202_out, not_203_out, not_204_out);
  and and_111 (and_111_out, not_205_out, not_206_out, not_207_out, not_208_out);
  and and_112 (and_112_out, not_209_out, B1, not_210_out);
  and and_113 (and_113_out, not_211_out, not_212_out, B2);
  and and_114 (and_114_out, not_213_out, B2, B0);
  and and_115 (and_115_out, B3, not_214_out, B0);
  and and_116 (and_116_out, not_215_out, B5, not_216_out, B1);
  and and_117 (and_117_out, not_217_out, B5, B2, B0);
  and and_118 (and_118_out, not_218_out, B5, B4, not_219_out, not_220_out);
  and and_119 (and_119_out, B6, not_221_out, not_222_out);
  and and_120 (and_120_out, B6, not_223_out, not_224_out, not_225_out);
  or or_1 (C_11, and_1_out, and_2_out, and_3_out, and_4_out, and_5_out, and_6_out, and_7_out, and_8_out, and_9_out, and_10_out, and_11_out, and_12_out, and_13_out);
  or or_2 (C_12, and_14_out, and_15_out, and_16_out, and_17_out, and_18_out, and_19_out, and_20_out, and_21_out, and_22_out, and_23_out, and_24_out, and_25_out, and_26_out);
  or or_3 (C_13, and_27_out, and_28_out, and_29_out, and_30_out, and_31_out, and_32_out, and_33_out, and_34_out, and_35_out, and_36_out, and_37_out, and_38_out, and_39_out, and_40_out);
  or or_4 (C_14, and_41_out, and_42_out, and_43_out, and_44_out, and_45_out, and_46_out, and_47_out, and_48_out, and_49_out, and_50_out, and_51_out, and_52_out, and_53_out, and_54_out, and_55_out);
  or or_5 (C_15, and_56_out, and_57_out, and_58_out, and_59_out, and_60_out, and_61_out, and_62_out, and_63_out, and_64_out, and_65_out, and_66_out);
  or or_6 (C_21, and_67_out, and_68_out, and_69_out, and_70_out, and_71_out, and_72_out, and_73_out, and_74_out, and_75_out, and_76_out, and_77_out, and_78_out, and_79_out, and_80_out);
  or or_7 (C_22, and_81_out, and_82_out, and_83_out, and_84_out, and_85_out, and_86_out);
  or or_8 (C_23, and_87_out, and_88_out, and_89_out, and_90_out, and_91_out, and_92_out, and_93_out, and_94_out, and_95_out, and_96_out, and_97_out, and_98_out, and_99_out, and_100_out, and_101_out);
  or or_9 (C_24, and_102_out, and_103_out, and_104_out, and_105_out, and_106_out, and_107_out, and_108_out, and_109_out);
  or or_10 (C_25, and_110_out, and_111_out, and_112_out, and_113_out, and_114_out, and_115_out, and_116_out, and_117_out, and_118_out, and_119_out, and_120_out);
endmodule

// ML2
module ASCII_7bits_2_5x5_Letter2 (
  input  B6,
  input  B5,
  input  B4,
  input  B3,
  input  B2,
  input  B1,
  input  B0,
  output C_31,
  output C_32,
  output C_33,
  output C_34,
  output C_35,
  output C_41,
  output C_42,
  output C_43,
  output C_44,
  output C_45
);

  wire and_1_out, and_2_out, and_3_out, and_4_out, and_5_out, and_6_out, and_7_out, and_8_out, and_9_out,
       and_10_out, and_11_out, and_12_out, and_13_out, and_14_out, and_15_out, and_16_out, and_17_out,
       and_18_out, and_19_out, and_20_out, and_21_out, and_22_out, and_23_out, and_24_out, and_25_out,
       and_26_out, and_27_out, and_28_out, and_29_out, and_30_out, and_31_out, and_32_out, and_33_out,
       and_34_out, and_35_out, and_36_out, and_37_out, and_38_out, and_39_out, and_40_out, and_41_out,
       and_42_out, and_43_out, and_44_out, and_45_out, and_46_out, and_47_out, and_48_out, and_49_out,
       and_50_out, and_51_out, and_52_out, and_53_out, and_54_out, and_55_out, and_56_out, and_57_out,
       and_58_out, and_59_out, and_60_out, and_61_out, and_62_out, and_63_out, and_64_out, and_65_out,
       and_66_out, and_67_out, and_68_out, and_69_out, and_70_out, and_71_out, and_72_out, and_73_out,
       and_74_out, and_75_out, and_76_out, and_77_out, and_78_out, and_79_out, and_80_out, and_81_out,
       and_82_out, and_83_out, and_84_out, and_85_out, and_86_out, and_87_out, and_88_out, and_89_out,
       and_90_out, and_91_out, and_92_out, and_93_out, and_94_out, and_95_out, and_96_out, and_97_out,
       and_98_out, and_99_out, and_100_out, and_101_out, and_102_out, and_103_out, and_104_out, and_105_out,
       and_106_out, and_107_out, and_108_out, and_109_out, and_110_out, and_111_out, and_112_out,
       and_113_out, and_114_out, and_115_out, and_116_out, and_117_out, and_118_out, and_119_out,
       and_120_out, and_121_out, and_122_out, and_123_out, and_124_out, and_125_out, and_126_out,
       and_127_out, and_128_out, not_1_out, not_2_out, not_3_out, not_4_out, not_5_out, not_6_out, not_7_out,
       not_8_out, not_9_out, not_10_out, not_11_out, not_12_out, not_13_out, not_14_out, not_15_out,
       not_16_out, not_17_out, not_18_out, not_19_out, not_20_out, not_21_out, not_22_out, not_23_out,
       not_24_out, not_25_out, not_26_out, not_27_out, not_28_out, not_29_out, not_30_out, not_31_out,
       not_32_out, not_33_out, not_34_out, not_35_out, not_36_out, not_37_out, not_38_out, not_39_out,
       not_40_out, not_41_out, not_42_out, not_43_out, not_44_out, not_45_out, not_46_out, not_47_out,
       not_48_out, not_49_out, not_50_out, not_51_out, not_52_out, not_53_out, not_54_out, not_55_out,
       not_56_out, not_57_out, not_58_out, not_59_out, not_60_out, not_61_out, not_62_out, not_63_out,
       not_64_out, not_65_out, not_66_out, not_67_out, not_68_out, not_69_out, not_70_out, not_71_out,
       not_72_out, not_73_out, not_74_out, not_75_out, not_76_out, not_77_out, not_78_out, not_79_out,
       not_80_out, not_81_out, not_82_out, not_83_out, not_84_out, not_85_out, not_86_out, not_87_out,
       not_88_out, not_89_out, not_90_out, not_91_out, not_92_out, not_93_out, not_94_out, not_95_out,
       not_96_out, not_97_out, not_98_out, not_99_out, not_100_out, not_101_out, not_102_out, not_103_out,
       not_104_out, not_105_out, not_106_out, not_107_out, not_108_out, not_109_out, not_110_out,
       not_111_out, not_112_out, not_113_out, not_114_out, not_115_out, not_116_out, not_117_out,
       not_118_out, not_119_out, not_120_out, not_121_out, not_122_out, not_123_out, not_124_out,
       not_125_out, not_126_out, not_127_out, not_128_out, not_129_out, not_130_out, not_131_out,
       not_132_out, not_133_out, not_134_out, not_135_out, not_136_out, not_137_out, not_138_out,
       not_139_out, not_140_out, not_141_out, not_142_out, not_143_out, not_144_out, not_145_out,
       not_146_out, not_147_out, not_148_out, not_149_out, not_150_out, not_151_out, not_152_out,
       not_153_out, not_154_out, not_155_out, not_156_out, not_157_out, not_158_out, not_159_out,
       not_160_out, not_161_out, not_162_out, not_163_out, not_164_out, not_165_out, not_166_out,
       not_167_out, not_168_out, not_169_out, not_170_out, not_171_out, not_172_out, not_173_out,
       not_174_out, not_175_out, not_176_out, not_177_out, not_178_out, not_179_out, not_180_out,
       not_181_out, not_182_out, not_183_out, not_184_out, not_185_out, not_186_out, not_187_out,
       not_188_out, not_189_out, not_190_out, not_191_out, not_192_out, not_193_out, not_194_out,
       not_195_out, not_196_out, not_197_out, not_198_out, not_199_out, not_200_out, not_201_out,
       not_202_out, not_203_out, not_204_out, not_205_out, not_206_out, not_207_out, not_208_out,
       not_209_out, not_210_out, not_211_out, not_212_out, not_213_out, not_214_out, not_215_out,
       not_216_out, not_217_out, not_218_out, not_219_out, not_220_out, not_221_out, not_222_out,
       not_223_out, not_224_out, not_225_out, not_226_out, not_227_out, not_228_out, not_229_out,
       not_230_out, not_231_out, not_232_out, not_233_out, not_234_out, not_235_out, not_236_out,
       not_237_out, not_238_out, not_239_out, not_240_out, not_241_out, not_242_out, not_243_out,
       not_244_out, not_245_out, not_246_out, not_247_out, not_248_out, not_249_out, not_250_out,
       not_251_out, not_252_out, not_253_out, not_254_out, not_255_out, not_256_out, not_257_out,
       not_258_out, not_259_out, not_260_out, not_261_out, not_262_out, not_263_out, not_264_out,
       not_265_out, not_266_out, not_267_out, not_268_out, not_269_out, not_270_out, not_271_out,
       not_272_out, not_273_out, not_274_out, not_275_out, not_276_out, not_277_out, not_278_out;

  not not_1 (not_1_out, B4);
  not not_2 (not_2_out, B3);
  not not_3 (not_3_out, B2);
  not not_4 (not_4_out, B5);
  not not_5 (not_5_out, B1);
  not not_6 (not_6_out, B0);
  not not_7 (not_7_out, B4);
  not not_8 (not_8_out, B3);
  not not_9 (not_9_out, B1);
  not not_10 (not_10_out, B4);
  not not_11 (not_11_out, B2);
  not not_12 (not_12_out, B1);
  not not_13 (not_13_out, B3);
  not not_14 (not_14_out, B1);
  not not_15 (not_15_out, B2);
  not not_16 (not_16_out, B0);
  not not_17 (not_17_out, B0);
  not not_18 (not_18_out, B6);
  not not_19 (not_19_out, B3);
  not not_20 (not_20_out, B6);
  not not_21 (not_21_out, B2);
  not not_22 (not_22_out, B1);
  not not_23 (not_23_out, B0);
  not not_24 (not_24_out, B4);
  not not_25 (not_25_out, B2);
  not not_26 (not_26_out, B1);
  not not_27 (not_27_out, B4);
  not not_28 (not_28_out, B2);
  not not_29 (not_29_out, B0);
  not not_30 (not_30_out, B5);
  not not_31 (not_31_out, B2);
  not not_32 (not_32_out, B1);
  not not_33 (not_33_out, B3);
  not not_34 (not_34_out, B2);
  not not_35 (not_35_out, B1);
  not not_36 (not_36_out, B5);
  not not_37 (not_37_out, B1);
  not not_38 (not_38_out, B0);
  not not_39 (not_39_out, B5);
  not not_40 (not_40_out, B3);
  not not_41 (not_41_out, B1);
  not not_42 (not_42_out, B0);
  not not_43 (not_43_out, B2);
  not not_44 (not_44_out, B1);
  not not_45 (not_45_out, B1);
  not not_46 (not_46_out, B0);
  not not_47 (not_47_out, B4);
  not not_48 (not_48_out, B1);
  not not_49 (not_49_out, B5);
  not not_50 (not_50_out, B4);
  not not_51 (not_51_out, B0);
  not not_52 (not_52_out, B4);
  not not_53 (not_53_out, B3);
  not not_54 (not_54_out, B0);
  not not_55 (not_55_out, B3);
  not not_56 (not_56_out, B2);
  not not_57 (not_57_out, B1);
  not not_58 (not_58_out, B0);
  not not_59 (not_59_out, B2);
  not not_60 (not_60_out, B6);
  not not_61 (not_61_out, B3);
  not not_62 (not_62_out, B6);
  not not_63 (not_63_out, B4);
  not not_64 (not_64_out, B0);
  not not_65 (not_65_out, B4);
  not not_66 (not_66_out, B1);
  not not_67 (not_67_out, B4);
  not not_68 (not_68_out, B2);
  not not_69 (not_69_out, B0);
  not not_70 (not_70_out, B5);
  not not_71 (not_71_out, B1);
  not not_72 (not_72_out, B0);
  not not_73 (not_73_out, B5);
  not not_74 (not_74_out, B1);
  not not_75 (not_75_out, B0);
  not not_76 (not_76_out, B6);
  not not_77 (not_77_out, B3);
  not not_78 (not_78_out, B2);
  not not_79 (not_79_out, B1);
  not not_80 (not_80_out, B1);
  not not_81 (not_81_out, B0);
  not not_82 (not_82_out, B5);
  not not_83 (not_83_out, B3);
  not not_84 (not_84_out, B1);
  not not_85 (not_85_out, B0);
  not not_86 (not_86_out, B4);
  not not_87 (not_87_out, B2);
  not not_88 (not_88_out, B1);
  not not_89 (not_89_out, B3);
  not not_90 (not_90_out, B2);
  not not_91 (not_91_out, B2);
  not not_92 (not_92_out, B0);
  not not_93 (not_93_out, B4);
  not not_94 (not_94_out, B3);
  not not_95 (not_95_out, B4);
  not not_96 (not_96_out, B6);
  not not_97 (not_97_out, B3);
  not not_98 (not_98_out, B6);
  not not_99 (not_99_out, B3);
  not not_100 (not_100_out, B6);
  not not_101 (not_101_out, B6);
  not not_102 (not_102_out, B2);
  not not_103 (not_103_out, B1);
  not not_104 (not_104_out, B3);
  not not_105 (not_105_out, B1);
  not not_106 (not_106_out, B0);
  not not_107 (not_107_out, B6);
  not not_108 (not_108_out, B4);
  not not_109 (not_109_out, B2);
  not not_110 (not_110_out, B6);
  not not_111 (not_111_out, B4);
  not not_112 (not_112_out, B3);
  not not_113 (not_113_out, B1);
  not not_114 (not_114_out, B6);
  not not_115 (not_115_out, B3);
  not not_116 (not_116_out, B1);
  not not_117 (not_117_out, B4);
  not not_118 (not_118_out, B2);
  not not_119 (not_119_out, B5);
  not not_120 (not_120_out, B4);
  not not_121 (not_121_out, B1);
  not not_122 (not_122_out, B0);
  not not_123 (not_123_out, B2);
  not not_124 (not_124_out, B6);
  not not_125 (not_125_out, B3);
  not not_126 (not_126_out, B0);
  not not_127 (not_127_out, B6);
  not not_128 (not_128_out, B2);
  not not_129 (not_129_out, B4);
  not not_130 (not_130_out, B3);
  not not_131 (not_131_out, B4);
  not not_132 (not_132_out, B1);
  not not_133 (not_133_out, B0);
  not not_134 (not_134_out, B4);
  not not_135 (not_135_out, B0);
  not not_136 (not_136_out, B2);
  not not_137 (not_137_out, B5);
  not not_138 (not_138_out, B0);
  not not_139 (not_139_out, B5);
  not not_140 (not_140_out, B3);
  not not_141 (not_141_out, B2);
  not not_142 (not_142_out, B1);
  not not_143 (not_143_out, B5);
  not not_144 (not_144_out, B3);
  not not_145 (not_145_out, B0);
  not not_146 (not_146_out, B0);
  not not_147 (not_147_out, B1);
  not not_148 (not_148_out, B0);
  not not_149 (not_149_out, B2);
  not not_150 (not_150_out, B6);
  not not_151 (not_151_out, B3);
  not not_152 (not_152_out, B1);
  not not_153 (not_153_out, B6);
  not not_154 (not_154_out, B2);
  not not_155 (not_155_out, B3);
  not not_156 (not_156_out, B2);
  not not_157 (not_157_out, B1);
  not not_158 (not_158_out, B3);
  not not_159 (not_159_out, B2);
  not not_160 (not_160_out, B0);
  not not_161 (not_161_out, B4);
  not not_162 (not_162_out, B3);
  not not_163 (not_163_out, B1);
  not not_164 (not_164_out, B0);
  not not_165 (not_165_out, B4);
  not not_166 (not_166_out, B2);
  not not_167 (not_167_out, B1);
  not not_168 (not_168_out, B0);
  not not_169 (not_169_out, B4);
  not not_170 (not_170_out, B3);
  not not_171 (not_171_out, B2);
  not not_172 (not_172_out, B3);
  not not_173 (not_173_out, B1);
  not not_174 (not_174_out, B5);
  not not_175 (not_175_out, B3);
  not not_176 (not_176_out, B2);
  not not_177 (not_177_out, B1);
  not not_178 (not_178_out, B0);
  not not_179 (not_179_out, B5);
  not not_180 (not_180_out, B4);
  not not_181 (not_181_out, B3);
  not not_182 (not_182_out, B1);
  not not_183 (not_183_out, B6);
  not not_184 (not_184_out, B4);
  not not_185 (not_185_out, B3);
  not not_186 (not_186_out, B0);
  not not_187 (not_187_out, B4);
  not not_188 (not_188_out, B3);
  not not_189 (not_189_out, B4);
  not not_190 (not_190_out, B2);
  not not_191 (not_191_out, B1);
  not not_192 (not_192_out, B0);
  not not_193 (not_193_out, B6);
  not not_194 (not_194_out, B2);
  not not_195 (not_195_out, B2);
  not not_196 (not_196_out, B6);
  not not_197 (not_197_out, B3);
  not not_198 (not_198_out, B0);
  not not_199 (not_199_out, B6);
  not not_200 (not_200_out, B3);
  not not_201 (not_201_out, B1);
  not not_202 (not_202_out, B6);
  not not_203 (not_203_out, B2);
  not not_204 (not_204_out, B6);
  not not_205 (not_205_out, B4);
  not not_206 (not_206_out, B3);
  not not_207 (not_207_out, B1);
  not not_208 (not_208_out, B3);
  not not_209 (not_209_out, B2);
  not not_210 (not_210_out, B1);
  not not_211 (not_211_out, B0);
  not not_212 (not_212_out, B3);
  not not_213 (not_213_out, B1);
  not not_214 (not_214_out, B4);
  not not_215 (not_215_out, B2);
  not not_216 (not_216_out, B2);
  not not_217 (not_217_out, B0);
  not not_218 (not_218_out, B6);
  not not_219 (not_219_out, B1);
  not not_220 (not_220_out, B0);
  not not_221 (not_221_out, B6);
  not not_222 (not_222_out, B4);
  not not_223 (not_223_out, B3);
  not not_224 (not_224_out, B2);
  not not_225 (not_225_out, B1);
  not not_226 (not_226_out, B3);
  not not_227 (not_227_out, B2);
  not not_228 (not_228_out, B0);
  not not_229 (not_229_out, B4);
  not not_230 (not_230_out, B3);
  not not_231 (not_231_out, B1);
  not not_232 (not_232_out, B0);
  not not_233 (not_233_out, B2);
  not not_234 (not_234_out, B1);
  not not_235 (not_235_out, B0);
  not not_236 (not_236_out, B2);
  not not_237 (not_237_out, B0);
  not not_238 (not_238_out, B1);
  not not_239 (not_239_out, B6);
  not not_240 (not_240_out, B5);
  not not_241 (not_241_out, B4);
  not not_242 (not_242_out, B3);
  not not_243 (not_243_out, B6);
  not not_244 (not_244_out, B4);
  not not_245 (not_245_out, B2);
  not not_246 (not_246_out, B0);
  not not_247 (not_247_out, B3);
  not not_248 (not_248_out, B2);
  not not_249 (not_249_out, B4);
  not not_250 (not_250_out, B1);
  not not_251 (not_251_out, B3);
  not not_252 (not_252_out, B1);
  not not_253 (not_253_out, B0);
  not not_254 (not_254_out, B5);
  not not_255 (not_255_out, B2);
  not not_256 (not_256_out, B2);
  not not_257 (not_257_out, B6);
  not not_258 (not_258_out, B3);
  not not_259 (not_259_out, B6);
  not not_260 (not_260_out, B3);
  not not_261 (not_261_out, B6);
  not not_262 (not_262_out, B6);
  not not_263 (not_263_out, B2);
  not not_264 (not_264_out, B1);
  not not_265 (not_265_out, B4);
  not not_266 (not_266_out, B2);
  not not_267 (not_267_out, B1);
  not not_268 (not_268_out, B0);
  not not_269 (not_269_out, B4);
  not not_270 (not_270_out, B4);
  not not_271 (not_271_out, B2);
  not not_272 (not_272_out, B0);
  not not_273 (not_273_out, B3);
  not not_274 (not_274_out, B1);
  not not_275 (not_275_out, B2);
  and and_1 (and_1_out, not_1_out, not_2_out, not_3_out, B1);
  and and_2 (and_2_out, not_4_out, B2, not_5_out, not_6_out);
  and and_3 (and_3_out, not_7_out, not_8_out, B2, not_9_out);
  and and_4 (and_4_out, not_10_out, B2, B1, B0);
  and and_5 (and_5_out, B3, not_11_out, not_12_out, B0);
  and and_6 (and_6_out, B4, not_13_out, not_14_out, B0);
  and and_7 (and_7_out, B4, not_15_out, B0);
  and and_8 (and_8_out, B4, B2, B1, not_16_out);
  and and_9 (and_9_out, B4, B3, B1);
  and and_10 (and_10_out, B4, B3, B2, not_17_out);
  and and_11 (and_11_out, not_18_out, B5, not_19_out, B0);
  and and_12 (and_12_out, not_20_out, B5, B4, not_21_out);
  and and_13 (and_13_out, B6, B2, not_22_out, not_23_out);
  and and_14 (and_14_out, not_24_out, B3, not_25_out, not_26_out, B0);
  and and_15 (and_15_out, not_27_out, B3, not_28_out, B1, not_29_out);
  and and_16 (and_16_out, not_30_out, B4, not_31_out, not_32_out, B0);
  and and_17 (and_17_out, B4, not_33_out, not_34_out, not_35_out, B0);
  and and_18 (and_18_out, not_36_out, B4, B2, not_37_out, not_38_out);
  and and_19 (and_19_out, not_39_out, B4, B2, B1, B0);
  and and_20 (and_20_out, B4, not_40_out, B2, B1, B0);
  and and_21 (and_21_out, B4, B3, B2, not_41_out, not_42_out);
  and and_22 (and_22_out, B6, B3, not_43_out, not_44_out, B0);
  and and_23 (and_23_out, B6, B4, B2, not_45_out, not_46_out);
  and and_24 (and_24_out, B6, B4, B2, B1, B0);
  and and_25 (and_25_out, not_47_out, not_48_out, B0);
  and and_26 (and_26_out, not_49_out, not_50_out, B1, not_51_out);
  and and_27 (and_27_out, not_52_out, not_53_out, B1, not_54_out);
  and and_28 (and_28_out, not_55_out, B2, B1, B0);
  and and_29 (and_29_out, B3, not_56_out);
  and and_30 (and_30_out, B4, not_57_out, not_58_out);
  and and_31 (and_31_out, B4, not_59_out, B1);
  and and_32 (and_32_out, not_60_out, B5, B4, not_61_out);
  and and_33 (and_33_out, not_62_out, B5, B4, B1, B0);
  and and_34 (and_34_out, B6, not_63_out, B1, not_64_out);
  and and_35 (and_35_out, not_65_out, B3, not_66_out, B0);
  and and_36 (and_36_out, not_67_out, B3, not_68_out, B1, not_69_out);
  and and_37 (and_37_out, not_70_out, B4, B2, not_71_out, not_72_out);
  and and_38 (and_38_out, not_73_out, B4, B2, B1, B0);
  and and_39 (and_39_out, B4, B3, B2, not_74_out, not_75_out);
  and and_40 (and_40_out, not_76_out, B5, not_77_out, not_78_out, not_79_out, B0);
  and and_41 (and_41_out, B6, B4, B2, not_80_out, not_81_out);
  and and_42 (and_42_out, B6, B4, B2, B1, B0);
  and and_43 (and_43_out, not_82_out, not_83_out, not_84_out, not_85_out);
  and and_44 (and_44_out, not_86_out, not_87_out, not_88_out, B0);
  and and_45 (and_45_out, not_89_out, not_90_out, B0);
  and and_46 (and_46_out, not_91_out, B1, not_92_out);
  and and_47 (and_47_out, not_93_out, not_94_out, B2);
  and and_48 (and_48_out, not_95_out, B2, B1, B0);
  and and_49 (and_49_out, not_96_out, B5, not_97_out, B0);
  and and_50 (and_50_out, not_98_out, B5, not_99_out, B1);
  and and_51 (and_51_out, not_100_out, B5, B2, B1, B0);
  and and_52 (and_52_out, not_101_out, B5, B4, not_102_out, not_103_out);
  and and_53 (and_53_out, B6, not_104_out, not_105_out, not_106_out);
  and and_54 (and_54_out, not_107_out, not_108_out, not_109_out, B1);
  not not_276 (not_276_out, B5);
  and and_55 (and_55_out, not_276_out, B1, B0);
  not not_277 (not_277_out, B4);
  and and_56 (and_56_out, not_277_out, B1, B0);
  and and_57 (and_57_out, not_110_out, not_111_out, not_112_out, B2, not_113_out);
  and and_58 (and_58_out, not_114_out, not_115_out, B2, not_116_out, B0);
  and and_59 (and_59_out, not_117_out, B3, not_118_out, B0);
  and and_60 (and_60_out, not_119_out, not_120_out, B3, B2, not_121_out, not_122_out);
  and and_61 (and_61_out, B4, B3, not_123_out, B1);
  and and_62 (and_62_out, not_124_out, B5, B4, not_125_out, not_126_out);
  and and_63 (and_63_out, not_127_out, B5, B4, not_128_out);
  and and_64 (and_64_out, B6, not_129_out, not_130_out, B0);
  and and_65 (and_65_out, B6, B1, B0);
  and and_66 (and_66_out, B6, not_131_out, B3, not_132_out, not_133_out);
  and and_67 (and_67_out, B6, not_134_out, B3, B2, not_135_out);
  and and_68 (and_68_out, B3, not_136_out, B1, B0);
  and and_69 (and_69_out, not_137_out, B3, B2, B1, not_138_out);
  and and_70 (and_70_out, not_139_out, B4, not_140_out, not_141_out, not_142_out, B0);
  and and_71 (and_71_out, not_143_out, B4, not_144_out, B1, not_145_out);
  and and_72 (and_72_out, B4, B2, B1, not_146_out);
  and and_73 (and_73_out, B4, B3, not_147_out, not_148_out);
  and and_74 (and_74_out, B5, B4, not_149_out, B1, B0);
  and and_75 (and_75_out, not_150_out, B5, B4, not_151_out, B2, not_152_out);
  and and_76 (and_76_out, not_153_out, B5, B4, B3, not_154_out, B0);
  and and_77 (and_77_out, B6, not_155_out, not_156_out, not_157_out, B0);
  and and_78 (and_78_out, B6, not_158_out, not_159_out, B1, not_160_out);
  and and_79 (and_79_out, B6, not_161_out, not_162_out, B2, not_163_out, not_164_out);
  and and_80 (and_80_out, B6, not_165_out, B2, B1, B0);
  and and_81 (and_81_out, B6, B3, not_166_out, not_167_out, not_168_out);
  and and_82 (and_82_out, B6, not_169_out, B3, B2, B1);
  and and_83 (and_83_out, B6, B4, not_170_out, not_171_out, B0);
  and and_84 (and_84_out, B6, B4, not_172_out, not_173_out, B0);
  and and_85 (and_85_out, not_174_out, not_175_out, not_176_out, not_177_out, not_178_out);
  and and_86 (and_86_out, not_179_out, not_180_out, not_181_out, not_182_out, B0);
  and and_87 (and_87_out, not_183_out, not_184_out, not_185_out, B1, not_186_out);
  and and_88 (and_88_out, not_187_out, not_188_out, B2, B0);
  and and_89 (and_89_out, not_189_out, B3, not_190_out, not_191_out, not_192_out);
  and and_90 (and_90_out, not_193_out, B4, not_194_out, B1, B0);
  and and_91 (and_91_out, B4, B3, not_195_out, B1, B0);
  and and_92 (and_92_out, not_196_out, B5, not_197_out, B1, not_198_out);
  and and_93 (and_93_out, not_199_out, B5, B4, not_200_out, B2, not_201_out);
  and and_94 (and_94_out, not_202_out, B5, B4, B3, not_203_out, B0);
  and and_95 (and_95_out, not_204_out, B5, B4, B3, B1, B0);
  and and_96 (and_96_out, B6, not_205_out, not_206_out, not_207_out);
  and and_97 (and_97_out, B6, not_208_out, not_209_out, not_210_out, not_211_out);
  and and_98 (and_98_out, B6, not_212_out, B2, not_213_out, B0);
  and and_99 (and_99_out, B6, not_214_out, B2, B1);
  and and_100 (and_100_out, B3, not_215_out, B1, B0);
  and and_101 (and_101_out, B4, not_216_out, B1, not_217_out);
  and and_102 (and_102_out, B4, B3);
  and and_103 (and_103_out, not_218_out, B5, B4, not_219_out, not_220_out);
  and and_104 (and_104_out, not_221_out, B5, B4, B1, B0);
  and and_105 (and_105_out, B6, not_222_out, not_223_out, not_224_out, not_225_out, B0);
  and and_106 (and_106_out, B6, not_226_out, not_227_out, B1, not_228_out);
  and and_107 (and_107_out, B6, not_229_out, not_230_out, B2, not_231_out, not_232_out);
  and and_108 (and_108_out, B6, B3, not_233_out, not_234_out, not_235_out);
  and and_109 (and_109_out, B6, B3, B2, B1);
  and and_110 (and_110_out, B6, B4, not_236_out, not_237_out);
  and and_111 (and_111_out, B6, B4, B2, not_238_out, B0);
  and and_112 (and_112_out, not_239_out, not_240_out, not_241_out, not_242_out);
  and and_113 (and_113_out, not_243_out, not_244_out, not_245_out, B1, not_246_out);
  and and_114 (and_114_out, not_247_out, not_248_out, B1, B0);
  not not_278 (not_278_out, B4);
  and and_115 (and_115_out, not_278_out, B2, B0);
  and and_116 (and_116_out, not_249_out, B3, not_250_out, B0);
  and and_117 (and_117_out, B4, not_251_out, not_252_out, not_253_out);
  and and_118 (and_118_out, not_254_out, B4, not_255_out, B0);
  and and_119 (and_119_out, B4, B3, not_256_out, B0);
  and and_120 (and_120_out, not_257_out, B5, not_258_out, B1);
  and and_121 (and_121_out, not_259_out, B5, not_260_out, B2);
  and and_122 (and_122_out, not_261_out, B5, B4, B1, B0);
  and and_123 (and_123_out, not_262_out, B5, B4, B3, not_263_out, not_264_out);
  and and_124 (and_124_out, B6, not_265_out, not_266_out, not_267_out, not_268_out);
  and and_125 (and_125_out, B6, not_269_out, B2, B1);
  and and_126 (and_126_out, B6, not_270_out, B3, not_271_out, not_272_out);
  and and_127 (and_127_out, B6, B4, not_273_out, not_274_out);
  and and_128 (and_128_out, B6, B4, B3, not_275_out, B1);
  or or_1 (C_31, and_1_out, and_2_out, and_3_out, and_4_out, and_5_out, and_6_out, and_7_out, and_8_out, and_9_out, and_10_out, and_11_out, and_12_out, and_13_out);
  or or_2 (C_32, and_14_out, and_15_out, and_16_out, and_17_out, and_18_out, and_19_out, and_20_out, and_21_out, and_22_out, and_23_out, and_24_out);
  or or_3 (C_33, and_25_out, and_26_out, and_27_out, and_28_out, and_29_out, and_30_out, and_31_out, and_32_out, and_33_out, and_34_out);
  or or_4 (C_34, and_35_out, and_36_out, and_37_out, and_38_out, and_39_out, and_40_out, and_41_out, and_42_out);
  or or_5 (C_35, and_43_out, and_44_out, and_45_out, and_46_out, and_47_out, and_48_out, and_49_out, and_50_out, and_51_out, and_52_out, and_53_out);
  or or_6 (C_41, and_54_out, and_55_out, and_56_out, and_57_out, and_58_out, and_59_out, and_60_out, and_61_out, and_62_out, and_63_out, and_64_out, and_65_out, and_66_out, and_67_out);
  or or_7 (C_42, and_68_out, and_69_out, and_70_out, and_71_out, and_72_out, and_73_out, and_74_out, and_75_out, and_76_out, and_77_out, and_78_out, and_79_out, and_80_out, and_81_out, and_82_out, and_83_out, and_84_out);
  or or_8 (C_43, and_85_out, and_86_out, and_87_out, and_88_out, and_89_out, and_90_out, and_91_out, and_92_out, and_93_out, and_94_out, and_95_out, and_96_out, and_97_out, and_98_out, and_99_out);
  or or_9 (C_44, and_100_out, and_101_out, and_102_out, and_103_out, and_104_out, and_105_out, and_106_out, and_107_out, and_108_out, and_109_out, and_110_out, and_111_out);
  or or_10 (C_45, and_112_out, and_113_out, and_114_out, and_115_out, and_116_out, and_117_out, and_118_out, and_119_out, and_120_out, and_121_out, and_122_out, and_123_out, and_124_out, and_125_out, and_126_out, and_127_out, and_128_out);
endmodule

// ML3
module ASCII_7bits_2_5x5_Letter3 (
  input  B6,
  input  B5,
  input  B4,
  input  B3,
  input  B2,
  input  B1,
  input  B0,
  output C_51,
  output C_52,
  output C_53,
  output C_54,
  output C_55
);

  wire and_1_out, and_2_out, and_3_out, and_4_out, and_5_out, and_6_out, and_7_out, and_8_out, and_9_out,
       and_10_out, and_11_out, and_12_out, and_13_out, and_14_out, and_15_out, and_16_out, and_17_out,
       and_18_out, and_19_out, and_20_out, and_21_out, and_22_out, and_23_out, and_24_out, and_25_out,
       and_26_out, and_27_out, and_28_out, and_29_out, and_30_out, and_31_out, and_32_out, and_33_out,
       and_34_out, and_35_out, and_36_out, and_37_out, and_38_out, and_39_out, and_40_out, and_41_out,
       and_42_out, and_43_out, and_44_out, and_45_out, and_46_out, and_47_out, and_48_out, and_49_out,
       and_50_out, and_51_out, and_52_out, and_53_out, and_54_out, and_55_out, and_56_out, and_57_out,
       and_58_out, and_59_out, and_60_out, and_61_out, and_62_out, and_63_out, and_64_out, and_65_out,
       and_66_out, and_67_out, and_68_out, and_69_out, and_70_out, and_71_out, and_72_out, and_73_out,
       not_1_out, not_2_out, not_3_out, not_4_out, not_5_out, not_6_out, not_7_out, not_8_out, not_9_out,
       not_10_out, not_11_out, not_12_out, not_13_out, not_14_out, not_15_out, not_16_out, not_17_out,
       not_18_out, not_19_out, not_20_out, not_21_out, not_22_out, not_23_out, not_24_out, not_25_out,
       not_26_out, not_27_out, not_28_out, not_29_out, not_30_out, not_31_out, not_32_out, not_33_out,
       not_34_out, not_35_out, not_36_out, not_37_out, not_38_out, not_39_out, not_40_out, not_41_out,
       not_42_out, not_43_out, not_44_out, not_45_out, not_46_out, not_47_out, not_48_out, not_49_out,
       not_50_out, not_51_out, not_52_out, not_53_out, not_54_out, not_55_out, not_56_out, not_57_out,
       not_58_out, not_59_out, not_60_out, not_61_out, not_62_out, not_63_out, not_64_out, not_65_out,
       not_66_out, not_67_out, not_68_out, not_69_out, not_70_out, not_71_out, not_72_out, not_73_out,
       not_74_out, not_75_out, not_76_out, not_77_out, not_78_out, not_79_out, not_80_out, not_81_out,
       not_82_out, not_83_out, not_84_out, not_85_out, not_86_out, not_87_out, not_88_out, not_89_out,
       not_90_out, not_91_out, not_92_out, not_93_out, not_94_out, not_95_out, not_96_out, not_97_out,
       not_98_out, not_99_out, not_100_out, not_101_out, not_102_out, not_103_out, not_104_out, not_105_out,
       not_106_out, not_107_out, not_108_out, not_109_out, not_110_out, not_111_out, not_112_out,
       not_113_out, not_114_out, not_115_out, not_116_out, not_117_out, not_118_out, not_119_out,
       not_120_out, not_121_out, not_122_out, not_123_out, not_124_out, not_125_out, not_126_out,
       not_127_out, not_128_out, not_129_out, not_130_out, not_131_out, not_132_out, not_133_out,
       not_134_out, not_135_out, not_136_out, not_137_out, not_138_out, not_139_out, not_140_out,
       not_141_out, not_142_out, not_143_out, not_144_out, not_145_out, not_146_out, not_147_out,
       not_148_out, not_149_out, not_150_out, not_151_out, not_152_out, not_153_out, not_154_out,
       not_155_out, not_156_out, not_157_out, not_158_out, not_159_out, not_160_out, not_161_out,
       not_162_out, not_163_out, not_164_out, not_165_out, not_166_out, not_167_out, not_168_out,
       not_169_out, not_170_out, not_171_out, not_172_out, not_173_out, not_174_out, not_175_out,
       not_176_out, not_177_out, not_178_out, not_179_out, not_180_out, not_181_out, not_182_out,
       not_183_out, not_184_out, not_185_out, not_186_out, not_187_out, not_188_out, not_189_out,
       not_190_out, not_191_out, not_192_out, not_193_out, not_194_out, not_195_out, not_196_out,
       not_197_out, not_198_out, not_199_out, not_200_out, not_201_out, not_202_out, not_203_out,
       not_204_out, not_205_out;

  not not_1 (not_1_out, B6);
  not not_2 (not_2_out, B5);
  not not_3 (not_3_out, B3);
  not not_4 (not_4_out, B2);
  not not_5 (not_5_out, B1);
  not not_6 (not_6_out, B6);
  not not_7 (not_7_out, B4);
  not not_8 (not_8_out, B6);
  not not_9 (not_9_out, B5);
  not not_10 (not_10_out, B2);
  not not_11 (not_11_out, B0);
  not not_12 (not_12_out, B6);
  not not_13 (not_13_out, B4);
  not not_14 (not_14_out, B2);
  not not_15 (not_15_out, B0);
  not not_16 (not_16_out, B4);
  not not_17 (not_17_out, B1);
  not not_18 (not_18_out, B6);
  not not_19 (not_19_out, B5);
  not not_20 (not_20_out, B6);
  not not_21 (not_21_out, B5);
  not not_22 (not_22_out, B2);
  not not_23 (not_23_out, B6);
  not not_24 (not_24_out, B0);
  not not_25 (not_25_out, B2);
  not not_26 (not_26_out, B5);
  not not_27 (not_27_out, B6);
  not not_28 (not_28_out, B3);
  not not_29 (not_29_out, B2);
  not not_30 (not_30_out, B1);
  not not_31 (not_31_out, B0);
  not not_32 (not_32_out, B3);
  not not_33 (not_33_out, B2);
  not not_34 (not_34_out, B1);
  not not_35 (not_35_out, B3);
  not not_36 (not_36_out, B2);
  not not_37 (not_37_out, B0);
  not not_38 (not_38_out, B2);
  not not_39 (not_39_out, B1);
  not not_40 (not_40_out, B0);
  not not_41 (not_41_out, B6);
  not not_42 (not_42_out, B5);
  not not_43 (not_43_out, B4);
  not not_44 (not_44_out, B3);
  not not_45 (not_45_out, B2);
  not not_46 (not_46_out, B1);
  not not_47 (not_47_out, B6);
  not not_48 (not_48_out, B4);
  not not_49 (not_49_out, B3);
  not not_50 (not_50_out, B2);
  not not_51 (not_51_out, B0);
  not not_52 (not_52_out, B6);
  not not_53 (not_53_out, B4);
  not not_54 (not_54_out, B3);
  not not_55 (not_55_out, B1);
  not not_56 (not_56_out, B0);
  not not_57 (not_57_out, B6);
  not not_58 (not_58_out, B4);
  not not_59 (not_59_out, B6);
  not not_60 (not_60_out, B4);
  not not_61 (not_61_out, B2);
  not not_62 (not_62_out, B1);
  not not_63 (not_63_out, B0);
  not not_64 (not_64_out, B1);
  not not_65 (not_65_out, B6);
  not not_66 (not_66_out, B5);
  not not_67 (not_67_out, B6);
  not not_68 (not_68_out, B5);
  not not_69 (not_69_out, B6);
  not not_70 (not_70_out, B5);
  not not_71 (not_71_out, B2);
  not not_72 (not_72_out, B0);
  not not_73 (not_73_out, B6);
  not not_74 (not_74_out, B3);
  not not_75 (not_75_out, B2);
  not not_76 (not_76_out, B1);
  not not_77 (not_77_out, B0);
  not not_78 (not_78_out, B4);
  not not_79 (not_79_out, B3);
  not not_80 (not_80_out, B2);
  not not_81 (not_81_out, B1);
  not not_82 (not_82_out, B0);
  not not_83 (not_83_out, B6);
  not not_84 (not_84_out, B5);
  not not_85 (not_85_out, B3);
  not not_86 (not_86_out, B2);
  not not_87 (not_87_out, B1);
  not not_88 (not_88_out, B6);
  not not_89 (not_89_out, B4);
  not not_90 (not_90_out, B3);
  not not_91 (not_91_out, B1);
  not not_92 (not_92_out, B6);
  not not_93 (not_93_out, B4);
  not not_94 (not_94_out, B6);
  not not_95 (not_95_out, B4);
  not not_96 (not_96_out, B2);
  not not_97 (not_97_out, B1);
  not not_98 (not_98_out, B0);
  not not_99 (not_99_out, B1);
  not not_100 (not_100_out, B6);
  not not_101 (not_101_out, B5);
  not not_102 (not_102_out, B6);
  not not_103 (not_103_out, B3);
  not not_104 (not_104_out, B2);
  not not_105 (not_105_out, B1);
  not not_106 (not_106_out, B0);
  not not_107 (not_107_out, B6);
  not not_108 (not_108_out, B5);
  not not_109 (not_109_out, B3);
  not not_110 (not_110_out, B5);
  not not_111 (not_111_out, B2);
  not not_112 (not_112_out, B0);
  not not_113 (not_113_out, B4);
  not not_114 (not_114_out, B3);
  not not_115 (not_115_out, B2);
  not not_116 (not_116_out, B1);
  not not_117 (not_117_out, B0);
  not not_118 (not_118_out, B3);
  not not_119 (not_119_out, B2);
  not not_120 (not_120_out, B1);
  not not_121 (not_121_out, B6);
  not not_122 (not_122_out, B5);
  not not_123 (not_123_out, B3);
  not not_124 (not_124_out, B2);
  not not_125 (not_125_out, B1);
  not not_126 (not_126_out, B6);
  not not_127 (not_127_out, B4);
  not not_128 (not_128_out, B3);
  not not_129 (not_129_out, B2);
  not not_130 (not_130_out, B0);
  not not_131 (not_131_out, B6);
  not not_132 (not_132_out, B4);
  not not_133 (not_133_out, B3);
  not not_134 (not_134_out, B1);
  not not_135 (not_135_out, B0);
  not not_136 (not_136_out, B6);
  not not_137 (not_137_out, B4);
  not not_138 (not_138_out, B2);
  not not_139 (not_139_out, B1);
  not not_140 (not_140_out, B0);
  not not_141 (not_141_out, B6);
  not not_142 (not_142_out, B4);
  not not_143 (not_143_out, B1);
  not not_144 (not_144_out, B6);
  not not_145 (not_145_out, B5);
  not not_146 (not_146_out, B6);
  not not_147 (not_147_out, B3);
  not not_148 (not_148_out, B2);
  not not_149 (not_149_out, B1);
  not not_150 (not_150_out, B0);
  not not_151 (not_151_out, B6);
  not not_152 (not_152_out, B5);
  not not_153 (not_153_out, B5);
  not not_154 (not_154_out, B0);
  not not_155 (not_155_out, B4);
  not not_156 (not_156_out, B3);
  not not_157 (not_157_out, B2);
  not not_158 (not_158_out, B1);
  not not_159 (not_159_out, B0);
  not not_160 (not_160_out, B3);
  not not_161 (not_161_out, B2);
  not not_162 (not_162_out, B6);
  not not_163 (not_163_out, B5);
  not not_164 (not_164_out, B2);
  not not_165 (not_165_out, B1);
  not not_166 (not_166_out, B0);
  not not_167 (not_167_out, B6);
  not not_168 (not_168_out, B4);
  not not_169 (not_169_out, B3);
  not not_170 (not_170_out, B6);
  not not_171 (not_171_out, B5);
  not not_172 (not_172_out, B6);
  not not_173 (not_173_out, B4);
  not not_174 (not_174_out, B3);
  not not_175 (not_175_out, B6);
  not not_176 (not_176_out, B4);
  not not_177 (not_177_out, B6);
  not not_178 (not_178_out, B4);
  not not_179 (not_179_out, B2);
  not not_180 (not_180_out, B0);
  not not_181 (not_181_out, B2);
  not not_182 (not_182_out, B6);
  not not_183 (not_183_out, B5);
  not not_184 (not_184_out, B3);
  not not_185 (not_185_out, B1);
  not not_186 (not_186_out, B6);
  not not_187 (not_187_out, B3);
  not not_188 (not_188_out, B2);
  not not_189 (not_189_out, B1);
  not not_190 (not_190_out, B0);
  not not_191 (not_191_out, B6);
  not not_192 (not_192_out, B5);
  not not_193 (not_193_out, B6);
  not not_194 (not_194_out, B0);
  not not_195 (not_195_out, B1);
  not not_196 (not_196_out, B4);
  not not_197 (not_197_out, B3);
  not not_198 (not_198_out, B2);
  not not_199 (not_199_out, B1);
  not not_200 (not_200_out, B0);
  not not_201 (not_201_out, B3);
  not not_202 (not_202_out, B2);
  not not_203 (not_203_out, B1);
  not not_204 (not_204_out, B1);
  not not_205 (not_205_out, B0);
  and and_1 (and_1_out, not_1_out, not_2_out, not_3_out, not_4_out, not_5_out, B0);
  and and_2 (and_2_out, not_6_out, not_7_out, B2, B0);
  and and_3 (and_3_out, not_8_out, not_9_out, B3, not_10_out, not_11_out);
  and and_4 (and_4_out, not_12_out, not_13_out, B3, not_14_out, not_15_out);
  and and_5 (and_5_out, not_16_out, B3, B2, not_17_out, B0);
  and and_6 (and_6_out, not_18_out, not_19_out, B3, B2, B1);
  and and_7 (and_7_out, not_20_out, not_21_out, B4, not_22_out, B1);
  and and_8 (and_8_out, not_23_out, B4, B3, B1, not_24_out);
  and and_9 (and_9_out, B4, B3, not_25_out, B1, B0);
  and and_10 (and_10_out, not_26_out, B4, B3, B2, B1);
  and and_11 (and_11_out, not_27_out, B5, B4, not_28_out, not_29_out, not_30_out, not_31_out);
  and and_12 (and_12_out, B6, B4, not_32_out, not_33_out, not_34_out, B0);
  and and_13 (and_13_out, B6, B4, not_35_out, not_36_out, B1, not_37_out);
  and and_14 (and_14_out, B6, B4, B3, not_38_out, not_39_out, not_40_out);
  and and_15 (and_15_out, B6, B4, B3, B2, B1);
  and and_16 (and_16_out, not_41_out, not_42_out, not_43_out, not_44_out, not_45_out, not_46_out);
  and and_17 (and_17_out, not_47_out, not_48_out, not_49_out, not_50_out, B1, not_51_out);
  and and_18 (and_18_out, not_52_out, not_53_out, not_54_out, B2, not_55_out, not_56_out);
  and and_19 (and_19_out, not_57_out, not_58_out, B2, B1, B0);
  and and_20 (and_20_out, not_59_out, not_60_out, B3, not_61_out, not_62_out, not_63_out);
  and and_21 (and_21_out, B3, B2, not_64_out, B0);
  and and_22 (and_22_out, not_65_out, not_66_out, B3, B2, B1);
  and and_23 (and_23_out, not_67_out, not_68_out, B4, B1, B0);
  and and_24 (and_24_out, not_69_out, not_70_out, B4, B2, B0);
  and and_25 (and_25_out, B4, B3, not_71_out, B1, B0);
  and and_26 (and_26_out, B4, B3, B2, B1, not_72_out);
  and and_27 (and_27_out, not_73_out, B5, B4, not_74_out, not_75_out, not_76_out, not_77_out);
  and and_28 (and_28_out, B6, not_78_out, not_79_out, not_80_out, not_81_out, not_82_out);
  and and_29 (and_29_out, B6, B4, B2, B1, B0);
  and and_30 (and_30_out, not_83_out, not_84_out, not_85_out, not_86_out, not_87_out);
  and and_31 (and_31_out, not_88_out, not_89_out, not_90_out, B2, not_91_out);
  and and_32 (and_32_out, not_92_out, not_93_out, B2, B0);
  and and_33 (and_33_out, not_94_out, not_95_out, B3, not_96_out, not_97_out, not_98_out);
  and and_34 (and_34_out, B3, B2, not_99_out, B0);
  and and_35 (and_35_out, not_100_out, not_101_out, B3, B2, B1);
  and and_36 (and_36_out, not_102_out, B4, not_103_out, not_104_out, not_105_out, not_106_out);
  and and_37 (and_37_out, not_107_out, not_108_out, B4, not_109_out, B0);
  and and_38 (and_38_out, not_110_out, B4, B2, B1);
  and and_39 (and_39_out, B4, B3, not_111_out, B1, B0);
  and and_40 (and_40_out, B4, B3, B2, B1, not_112_out);
  and and_41 (and_41_out, B6, not_113_out, not_114_out, not_115_out, not_116_out, not_117_out);
  and and_42 (and_42_out, B6, B4, not_118_out, not_119_out, not_120_out, B0);
  and and_43 (and_43_out, B6, B4, B2, B1);
  and and_44 (and_44_out, not_121_out, not_122_out, not_123_out, not_124_out, not_125_out);
  and and_45 (and_45_out, not_126_out, not_127_out, not_128_out, not_129_out, B1, not_130_out);
  and and_46 (and_46_out, not_131_out, not_132_out, not_133_out, B2, not_134_out, not_135_out);
  and and_47 (and_47_out, not_136_out, not_137_out, B3, not_138_out, not_139_out, not_140_out);
  and and_48 (and_48_out, not_141_out, not_142_out, B3, B2, B0);
  and and_49 (and_49_out, B3, B2, not_143_out, B0);
  and and_50 (and_50_out, not_144_out, not_145_out, B3, B2, B1);
  and and_51 (and_51_out, not_146_out, B4, not_147_out, not_148_out, not_149_out, not_150_out);
  and and_52 (and_52_out, not_151_out, not_152_out, B4, B2, B0);
  and and_53 (and_53_out, not_153_out, B4, B2, B1);
  and and_54 (and_54_out, B4, B3, B2, B1, not_154_out);
  and and_55 (and_55_out, B6, not_155_out, not_156_out, not_157_out, not_158_out, not_159_out);
  and and_56 (and_56_out, B6, B4, not_160_out, not_161_out, B0);
  and and_57 (and_57_out, B6, B4, B2, B1);
  and and_58 (and_58_out, not_162_out, not_163_out, not_164_out, not_165_out, not_166_out);
  and and_59 (and_59_out, not_167_out, not_168_out, not_169_out, B2, B0);
  and and_60 (and_60_out, not_170_out, not_171_out, B2, B1);
  and and_61 (and_61_out, not_172_out, not_173_out, not_174_out, B2, B1);
  and and_62 (and_62_out, not_175_out, not_176_out, B2, B1, B0);
  and and_63 (and_63_out, not_177_out, not_178_out, B3, not_179_out, not_180_out);
  and and_64 (and_64_out, B3, not_181_out, B1, B0);
  and and_65 (and_65_out, not_182_out, not_183_out, B4, not_184_out, not_185_out);
  and and_66 (and_66_out, not_186_out, B4, not_187_out, not_188_out, not_189_out, not_190_out);
  and and_67 (and_67_out, not_191_out, not_192_out, B4, B1, B0);
  and and_68 (and_68_out, not_193_out, B4, B3, B1, not_194_out);
  and and_69 (and_69_out, B4, B3, B2, not_195_out);
  and and_70 (and_70_out, B6, not_196_out, not_197_out, not_198_out, not_199_out, not_200_out);
  and and_71 (and_71_out, B6, B4, not_201_out, not_202_out, not_203_out, B0);
  and and_72 (and_72_out, B6, B4, B2, B1);
  and and_73 (and_73_out, B6, B4, B3, not_204_out, not_205_out);
  or or_1 (C_51, and_1_out, and_2_out, and_3_out, and_4_out, and_5_out, and_6_out, and_7_out, and_8_out, and_9_out, and_10_out, and_11_out, and_12_out, and_13_out, and_14_out, and_15_out);
  or or_2 (C_52, and_16_out, and_17_out, and_18_out, and_19_out, and_20_out, and_21_out, and_22_out, and_23_out, and_24_out, and_25_out, and_26_out, and_27_out, and_28_out, and_29_out);
  or or_3 (C_53, and_30_out, and_31_out, and_32_out, and_33_out, and_34_out, and_35_out, and_36_out, and_37_out, and_38_out, and_39_out, and_40_out, and_41_out, and_42_out, and_43_out);
  or or_4 (C_54, and_44_out, and_45_out, and_46_out, and_47_out, and_48_out, and_49_out, and_50_out, and_51_out, and_52_out, and_53_out, and_54_out, and_55_out, and_56_out, and_57_out);
  or or_5 (C_55, and_58_out, and_59_out, and_60_out, and_61_out, and_62_out, and_63_out, and_64_out, and_65_out, and_66_out, and_67_out, and_68_out, and_69_out, and_70_out, and_71_out, and_72_out, and_73_out);
endmodule

// DC7-ML
module decod_ASCII7bits_2_5x5MatrixLetter (
  input  [6:0] _7bits,
  output [4:0] COL1,
  output [4:0] COL2,
  output [4:0] COL3,
  output [4:0] COL4,
  output [4:0] COL5
);

  ASCII_7bits_2_5x5_Letter ascii_7bits_2_5x5_letter_1 (
    .B6(_7bits[6]), .B5(_7bits[5]), .B4(_7bits[4]), .B3(_7bits[3]), .B2(_7bits[2]), .B1(_7bits[1]),
    .B0(_7bits[0]), .C_11(COL1[0]), .C_12(COL1[1]), .C_13(COL1[2]), .C_14(COL1[3]), .C_15(COL1[4]),
    .C_21(COL2[0]), .C_22(COL2[1]), .C_23(COL2[2]), .C_24(COL2[3]), .C_25(COL2[4]));
  ASCII_7bits_2_5x5_Letter2 ascii_7bits_2_5x5_letter2_1 (
    .B6(_7bits[6]), .B5(_7bits[5]), .B4(_7bits[4]), .B3(_7bits[3]), .B2(_7bits[2]), .B1(_7bits[1]),
    .B0(_7bits[0]), .C_31(COL3[0]), .C_32(COL3[1]), .C_33(COL3[2]), .C_34(COL3[3]), .C_35(COL3[4]),
    .C_41(COL4[0]), .C_42(COL4[1]), .C_43(COL4[2]), .C_44(COL4[3]), .C_45(COL4[4]));
  ASCII_7bits_2_5x5_Letter3 ascii_7bits_2_5x5_letter3_1 (
    .B6(_7bits[6]), .B5(_7bits[5]), .B4(_7bits[4]), .B3(_7bits[3]), .B2(_7bits[2]), .B1(_7bits[1]),
    .B0(_7bits[0]), .C_51(COL5[0]), .C_52(COL5[1]), .C_53(COL5[2]), .C_54(COL5[3]), .C_55(COL5[4]));
endmodule

// MUX
module Mux_2 (
  input  F1,
  input  F3,
  input  VelSwitcher,
  output S
);

  wire and_1_out, and_2_out;

  and and_1 (and_1_out, F1, ~VelSwitcher);  // AND_Gate
  and and_2 (and_2_out, F3, VelSwitcher);
  or or_1 (S, and_1_out, and_2_out);
endmodule

module FreqDiv (
  input  CK,
  input  CLR,
  output F1,
  output F2,
  output F3,
  output F4
);

  and and_1 (F1, ~CLR, CK);  // AND_Gate
  T_Flip_Flop t_ff_1 (.clk(CK), .T(1'b1), .Q(F2), .reset(CLR));  // open: Qn, preset, en
  T_Flip_Flop t_ff_2 (.clk(F2), .T(1'b1), .Q(F3), .reset(CLR));  // open: Qn, preset, en
  T_Flip_Flop t_ff_3 (.clk(F3), .T(1'b1), .Q(F4), .reset(CLR));  // open: Qn, preset, en
endmodule

// VSwi
module VelSwitcher (
  input  Vel_Switcher,
  input  CK,
  input  Pause,
  output CK_Vel
);

  wire freqdiv_1_f1, freqdiv_1_f3, mux_2_1_s, t_ff_1_q;

  T_Flip_Flop #(.trigger("falling")) t_ff_1 (
    .clk(Vel_Switcher), .T(1'b1), .Q(t_ff_1_q));  // open: Qn, preset, reset, en
  and and_1 (CK_Vel, ~Pause, mux_2_1_s);  // AND_Gate
  Mux_2 mux_2_1 (.F1(freqdiv_1_f1), .F3(freqdiv_1_f3), .VelSwitcher(t_ff_1_q), .S(mux_2_1_s));
  FreqDiv freqdiv_1 (.CK(CK), .CLR(Pause), .F1(freqdiv_1_f1), .F3(freqdiv_1_f3));  // open: F2, F4
endmodule
